# Fritzing sketch arduino1sketch (saved by Fritzing 0.9.3b)
breadboards: 1

parts:
  Componente1 = Arduino Uno (Rev3) - ICSP
  Componente2 = NRF24L01+ Breakout Board
  U1 = RFID RC522 SIP - 8 pins [chip_label="RFID RC522" package="SIP (Single Inline) [THT]"]

nets:
  N1: Componente1.D9_PWM, U1.RST
  N2: Componente1.D10_PWM/SS, U1.NSS
  N3: Componente1.D11_PWM/MOSI, Componente2.MOSI, U1.MOSI
  N4: Componente1.D12/MISO, Componente2.MISO, U1.MISO
  N5: Componente1.D13/SCK, Componente2.SCK, U1.SCK
  N6: Componente1.D5_PWM, Componente2.CE
  N7: Componente1.D6_PWM, Componente2.CS
  VCC: Componente1.3V3, Componente2.VCC, U1.VCC
  GND: Componente1.GND, Componente2.GND, U1.GND

custom parts:
  RFID RC522 SIP - 8 pins: A SIP stand-in part for RFID RC522 . With 8 pins on a 300 mil single inline package (SIP) footprint.
