# Fritzing sketch arduino2sketch (saved by Fritzing 0.9.3b)
breadboards: 1

parts:
  Componente1 = Arduino Mega ADK (Rev3)
  Componente2 = NRF24L01+ Breakout Board
  U1 = RFID RC522 SIP - 8 pins [chip_label="RFID RC522" package="SIP (Single Inline) [THT]"]
  Componente3 = Zeta LCD keypad shield for Arduino

nets:
  N1: Componente1.A0, Componente3.A0
  N2: Componente1.D20/SDA, U1.NSS
  GND: Componente1.GND, Componente2.GND, U1.GND, Componente3.D10_SS, Componente3.GND
  N3: Componente1.D9_PWM, Componente3.D9
  N4: Componente1.D8_PWM, Componente3.D8
  VCC: Componente1.3V3, Componente2.VCC, U1.VCC
  5V: Componente1.5V, Componente3.+5V
  N5: Componente1.D4_PWM, Componente3.D4
  N6: Componente1.D5_PWM, Componente3.D5
  N7: Componente1.D6_PWM, Componente3.D6
  N8: Componente1.D7_PWM, Componente3.D7
  N9: Componente1.D24, U1.RST
  N10: Componente1.D30, Componente2.CE
  N11: Componente1.D31, Componente2.CS
  N12: Componente1.D50/MISO, Componente2.MISO, U1.MISO
  N13: Componente1.D51/MOSI, Componente2.MOSI, U1.MOSI
  N14: Componente1.D52/SCK, Componente2.SCK, U1.SCK

custom parts:
  RFID RC522 SIP - 8 pins: A SIP stand-in part for RFID RC522 . With 8 pins on a 300 mil single inline package (SIP) footprint.
  Zeta LCD keypad shield for Arduino: The LCD shield for Arduino
